// Logisim project 19-bit-ALU-updated.circ as structural Verilog: 11 circuits, main circuit main
module main (
  input  [2:0] Control,
  input  [18:0] A,
  input  [18:0] B,
  input  Reset,
  input  clk,
  output [18:0] Upper_25,
  output [18:0] Lower_25,
  output Zero,
  output Negative,
  output Overflow,
  output Carry,
  output [4:0] counter_state
);

  _19_bit_ALU u_19_bit_alu_1 (
    .A(A), .B(B), .Lower_25(Lower_25), .Zero(Zero), .Negative(Negative), .Overflow(Overflow), .Carry(Carry),
    .Control0(Control[0]), .Control1(Control[1]), .Reset(Reset), .Control2(Control[2]), .Upper_25(Upper_25),
    .Clk(clk), .counter_state(counter_state));
endmodule

// 19-bit AND
module _19_bit_AND (
  input  [18:0] A,
  input  [18:0] B,
  output [18:0] Result
);

  wire and_20_out, and_21_out, and_22_out, and_23_out, and_24_out, and_25_out, undriven, undriven_2,
       undriven_3, undriven_4, undriven_5, undriven_6, undriven_7, undriven_8, undriven_9, undriven_10,
       undriven_11, undriven_12;

  and and_1 (Result[0], undriven, undriven_11);
  and and_2 (Result[1], undriven_2, undriven_7);
  and and_3 (Result[2], undriven_3, undriven_8);
  and and_4 (Result[3], undriven_12, undriven_4);
  and and_5 (Result[4], undriven_5, undriven_9);
  and and_6 (Result[5], undriven_6, undriven_10);
  and and_7 (Result[6], A[0], B[0]);
  and and_8 (Result[7], A[1], B[1]);
  and and_9 (Result[8], A[2], B[2]);
  and and_10 (Result[9], A[3], B[3]);
  and and_11 (Result[10], A[4], B[4]);
  and and_12 (Result[11], A[5], B[5]);
  and and_13 (Result[12], A[6], B[6]);
  and and_14 (Result[13], A[7], B[7]);
  and and_15 (Result[14], A[8], B[8]);
  and and_16 (Result[15], A[9], B[9]);
  and and_17 (Result[16], A[10], B[10]);
  and and_18 (Result[17], A[11], B[11]);
  and and_19 (Result[18], A[12], B[12]);
  and and_20 (and_20_out, A[13], B[13]);
  and and_21 (and_21_out, A[14], B[14]);
  and and_22 (and_22_out, A[15], B[15]);
  and and_23 (and_23_out, A[16], B[16]);
  and and_24 (and_24_out, A[17], B[17]);
  and and_25 (and_25_out, A[18], B[18]);
endmodule

// 19-bit OR
module _19_bit_OR (
  input  [18:0] A,
  input  [18:0] B,
  output [18:0] Result
);

  wire or_19_out, or_20_out, or_21_out, or_22_out, or_23_out, or_24_out, undriven, undriven_2, undriven_3,
       undriven_4, undriven_5, undriven_6, undriven_7, undriven_8, undriven_9, undriven_10, undriven_11,
       undriven_12;

  or or_1 (Result[1], undriven_2, undriven_7);
  or or_2 (Result[2], undriven_3, undriven_8);
  or or_3 (Result[3], undriven_12, undriven_4);
  or or_4 (Result[4], undriven_5, undriven_9);
  or or_5 (Result[5], undriven_6, undriven_10);
  or or_6 (Result[6], A[0], B[0]);
  or or_7 (Result[7], A[1], B[1]);
  or or_8 (Result[8], A[2], B[2]);
  or or_9 (Result[9], A[3], B[3]);
  or or_10 (Result[10], A[4], B[4]);
  or or_11 (Result[11], A[5], B[5]);
  or or_12 (Result[12], A[6], B[6]);
  or or_13 (Result[13], A[7], B[7]);
  or or_14 (Result[14], A[8], B[8]);
  or or_15 (Result[15], A[9], B[9]);
  or or_16 (Result[16], A[10], B[10]);
  or or_17 (Result[17], A[11], B[11]);
  or or_18 (Result[18], A[12], B[12]);
  or or_19 (or_19_out, A[13], B[13]);
  or or_20 (or_20_out, A[14], B[14]);
  or or_21 (or_21_out, A[15], B[15]);
  or or_22 (or_22_out, A[16], B[16]);
  or or_23 (or_23_out, A[17], B[17]);
  or or_24 (or_24_out, A[18], B[18]);
  or or_25 (Result[0], undriven, undriven_11);
endmodule

module Full_adder (
  input  Carry_in,
  input  A,
  input  B,
  output Result,
  output Carry_out
);

  wire and_1_out, and_2_out, xor_1_out;

  and and_1 (and_1_out, B, A);
  xor xor_1 (xor_1_out, A, B);
  or or_1 (Carry_out, and_1_out, and_2_out);
  and and_2 (and_2_out, xor_1_out, Carry_in);
  xor xor_2 (Result, Carry_in, xor_1_out);
endmodule

module _19_bit_full_adder (
  input  Carry_in,
  input  A0,
  input  B0,
  input  A1,
  input  B1,
  input  A2,
  input  B2,
  input  A3,
  input  B3,
  input  A4,
  input  B4,
  input  A5,
  input  B5,
  input  A6,
  input  B6,
  input  A7,
  input  B7,
  input  A8,
  input  B8,
  input  A9,
  input  B9,
  input  A10,
  input  B10,
  input  A11,
  input  B11,
  input  A12,
  input  B12,
  input  A13,
  input  B13,
  input  A14,
  input  B14,
  input  A15,
  input  B15,
  input  A16,
  input  B16,
  input  A17,
  input  B17,
  input  A18,
  input  B18,
  input  A19,
  input  B19,
  input  A20,
  input  B20,
  input  A21,
  input  B21,
  input  A22,
  input  B22,
  input  A23,
  input  B23,
  input  A24,
  input  B24,
  output Result0,
  output Result1,
  output Result2,
  output Result3,
  output Result4,
  output Result5,
  output Result6,
  output Result7,
  output Result8,
  output Result9,
  output Result10,
  output Result11,
  output Result12,
  output Result13,
  output Result14,
  output Result15,
  output Result16,
  output Result17,
  output Result18,
  output Result19,
  output Result20,
  output Result21,
  output Result22,
  output Result23,
  output Result24,
  output Carry
);

  wire full_adder_1_carry_out, full_adder_2_carry_out, full_adder_3_carry_out, full_adder_4_carry_out,
       full_adder_5_carry_out, full_adder_6_carry_out, full_adder_7_carry_out, full_adder_8_carry_out,
       full_adder_9_carry_out, full_adder_10_carry_out, full_adder_11_carry_out, full_adder_12_carry_out,
       full_adder_13_carry_out, full_adder_14_carry_out, full_adder_15_carry_out, full_adder_16_carry_out,
       full_adder_17_carry_out, full_adder_18_carry_out, full_adder_19_carry_out, full_adder_20_carry_out,
       full_adder_21_carry_out, full_adder_22_carry_out, full_adder_23_carry_out, full_adder_24_carry_out;

  Full_adder full_adder_1 (.Carry_in(Carry_in), .A(A0), .B(B0), .Result(Result0), .Carry_out(full_adder_1_carry_out));
  Full_adder full_adder_2 (
    .Carry_in(full_adder_1_carry_out), .A(A1), .B(B1), .Result(Result1), .Carry_out(full_adder_2_carry_out));
  Full_adder full_adder_3 (
    .Carry_in(full_adder_2_carry_out), .A(A2), .B(B2), .Result(Result2), .Carry_out(full_adder_3_carry_out));
  Full_adder full_adder_4 (
    .Carry_in(full_adder_3_carry_out), .A(A3), .B(B3), .Result(Result3), .Carry_out(full_adder_4_carry_out));
  Full_adder full_adder_5 (
    .Carry_in(full_adder_4_carry_out), .A(A4), .B(B4), .Result(Result4), .Carry_out(full_adder_5_carry_out));
  Full_adder full_adder_6 (
    .Carry_in(full_adder_5_carry_out), .A(A5), .B(B5), .Result(Result5), .Carry_out(full_adder_6_carry_out));
  Full_adder full_adder_7 (
    .Carry_in(full_adder_6_carry_out), .A(A6), .B(B6), .Result(Result6), .Carry_out(full_adder_7_carry_out));
  Full_adder full_adder_8 (
    .Carry_in(full_adder_7_carry_out), .A(A7), .B(B7), .Result(Result7), .Carry_out(full_adder_8_carry_out));
  Full_adder full_adder_9 (
    .Carry_in(full_adder_8_carry_out), .A(A8), .B(B8), .Result(Result8), .Carry_out(full_adder_9_carry_out));
  Full_adder full_adder_10 (
    .Carry_in(full_adder_9_carry_out), .A(A9), .B(B9), .Result(Result9), .Carry_out(full_adder_10_carry_out));
  Full_adder full_adder_11 (
    .Carry_in(full_adder_10_carry_out), .A(A10), .B(B10), .Result(Result10),
    .Carry_out(full_adder_11_carry_out));
  Full_adder full_adder_12 (
    .Carry_in(full_adder_11_carry_out), .A(A11), .B(B11), .Result(Result11),
    .Carry_out(full_adder_12_carry_out));
  Full_adder full_adder_13 (
    .Carry_in(full_adder_12_carry_out), .A(A12), .B(B12), .Result(Result12),
    .Carry_out(full_adder_13_carry_out));
  Full_adder full_adder_14 (
    .Carry_in(full_adder_13_carry_out), .A(A13), .B(B13), .Result(Result13),
    .Carry_out(full_adder_14_carry_out));
  Full_adder full_adder_15 (
    .Carry_in(full_adder_14_carry_out), .A(A14), .B(B14), .Result(Result14),
    .Carry_out(full_adder_15_carry_out));
  Full_adder full_adder_16 (
    .Carry_in(full_adder_15_carry_out), .A(A15), .B(B15), .Result(Result15),
    .Carry_out(full_adder_16_carry_out));
  Full_adder full_adder_17 (
    .Carry_in(full_adder_16_carry_out), .A(A16), .B(B16), .Result(Result16),
    .Carry_out(full_adder_17_carry_out));
  Full_adder full_adder_18 (
    .Carry_in(full_adder_17_carry_out), .A(A17), .B(B17), .Result(Result17),
    .Carry_out(full_adder_18_carry_out));
  Full_adder full_adder_19 (
    .Carry_in(full_adder_18_carry_out), .A(A18), .B(B18), .Result(Result18),
    .Carry_out(full_adder_19_carry_out));
  Full_adder full_adder_20 (
    .Carry_in(full_adder_19_carry_out), .A(A19), .B(B19), .Result(Result19),
    .Carry_out(full_adder_20_carry_out));
  Full_adder full_adder_21 (
    .Carry_in(full_adder_20_carry_out), .A(A20), .B(B20), .Result(Result20),
    .Carry_out(full_adder_21_carry_out));
  Full_adder full_adder_22 (
    .Carry_in(full_adder_21_carry_out), .A(A21), .B(B21), .Result(Result21),
    .Carry_out(full_adder_22_carry_out));
  Full_adder full_adder_23 (
    .Carry_in(full_adder_22_carry_out), .A(A22), .B(B22), .Result(Result22),
    .Carry_out(full_adder_23_carry_out));
  Full_adder full_adder_24 (
    .Carry_in(full_adder_23_carry_out), .A(A23), .B(B23), .Result(Result23),
    .Carry_out(full_adder_24_carry_out));
  Full_adder full_adder_25 (.Carry_in(full_adder_24_carry_out), .A(A24), .B(B24), .Result(Result24), .Carry_out(Carry));
endmodule

// FA
module _19_bit_full_adder_concise (
  input  Carry_in,
  input  [18:0] A,
  input  [18:0] B,
  output [18:0] Result,
  output Carry
);

  wire full_adder_1_carry_out, full_adder_2_carry_out, full_adder_3_carry_out, full_adder_4_carry_out,
       full_adder_5_carry_out, full_adder_6_carry_out, full_adder_7_carry_out, full_adder_8_carry_out,
       full_adder_9_carry_out, full_adder_10_carry_out, full_adder_11_carry_out, full_adder_12_carry_out,
       full_adder_13_carry_out, full_adder_14_carry_out, full_adder_15_carry_out, full_adder_16_carry_out,
       full_adder_17_carry_out, full_adder_18_carry_out, full_adder_19_carry_out, full_adder_20_carry_out,
       full_adder_20_result, full_adder_21_carry_out, full_adder_21_result, full_adder_22_carry_out,
       full_adder_22_result, full_adder_23_carry_out, full_adder_23_result, full_adder_24_carry_out,
       full_adder_24_result, full_adder_25_result, undriven, undriven_2, undriven_3, undriven_4, undriven_5,
       undriven_6, undriven_7, undriven_8, undriven_9, undriven_10, undriven_11, undriven_12;

  Full_adder full_adder_1 (
    .Carry_in(Carry_in), .A(undriven_5), .B(undriven_11), .Result(Result[0]),
    .Carry_out(full_adder_1_carry_out));
  Full_adder full_adder_2 (
    .Carry_in(full_adder_1_carry_out), .A(undriven_6), .B(undriven), .Result(Result[1]),
    .Carry_out(full_adder_2_carry_out));
  Full_adder full_adder_3 (
    .Carry_in(full_adder_2_carry_out), .A(undriven_7), .B(undriven_2), .Result(Result[2]),
    .Carry_out(full_adder_3_carry_out));
  Full_adder full_adder_4 (
    .Carry_in(full_adder_3_carry_out), .A(undriven_8), .B(undriven_12), .Result(Result[3]),
    .Carry_out(full_adder_4_carry_out));
  Full_adder full_adder_5 (
    .Carry_in(full_adder_4_carry_out), .A(undriven_9), .B(undriven_3), .Result(Result[4]),
    .Carry_out(full_adder_5_carry_out));
  Full_adder full_adder_6 (
    .Carry_in(full_adder_5_carry_out), .A(undriven_10), .B(undriven_4), .Result(Result[5]),
    .Carry_out(full_adder_6_carry_out));
  Full_adder full_adder_7 (
    .Carry_in(full_adder_6_carry_out), .A(A[0]), .B(B[0]), .Result(Result[6]),
    .Carry_out(full_adder_7_carry_out));
  Full_adder full_adder_8 (
    .Carry_in(full_adder_7_carry_out), .A(A[1]), .B(B[1]), .Result(Result[7]),
    .Carry_out(full_adder_8_carry_out));
  Full_adder full_adder_9 (
    .Carry_in(full_adder_8_carry_out), .A(A[2]), .B(B[2]), .Result(Result[8]),
    .Carry_out(full_adder_9_carry_out));
  Full_adder full_adder_10 (
    .Carry_in(full_adder_9_carry_out), .A(A[3]), .B(B[3]), .Result(Result[9]),
    .Carry_out(full_adder_10_carry_out));
  Full_adder full_adder_11 (
    .Carry_in(full_adder_10_carry_out), .A(A[4]), .B(B[4]), .Result(Result[10]),
    .Carry_out(full_adder_11_carry_out));
  Full_adder full_adder_12 (
    .Carry_in(full_adder_11_carry_out), .A(A[5]), .B(B[5]), .Result(Result[11]),
    .Carry_out(full_adder_12_carry_out));
  Full_adder full_adder_13 (
    .Carry_in(full_adder_12_carry_out), .A(A[6]), .B(B[6]), .Result(Result[12]),
    .Carry_out(full_adder_13_carry_out));
  Full_adder full_adder_14 (
    .Carry_in(full_adder_13_carry_out), .A(A[7]), .B(B[7]), .Result(Result[13]),
    .Carry_out(full_adder_14_carry_out));
  Full_adder full_adder_15 (
    .Carry_in(full_adder_14_carry_out), .A(A[8]), .B(B[8]), .Result(Result[14]),
    .Carry_out(full_adder_15_carry_out));
  Full_adder full_adder_16 (
    .Carry_in(full_adder_15_carry_out), .A(A[9]), .B(B[9]), .Result(Result[15]),
    .Carry_out(full_adder_16_carry_out));
  Full_adder full_adder_17 (
    .Carry_in(full_adder_16_carry_out), .A(A[10]), .B(B[10]), .Result(Result[16]),
    .Carry_out(full_adder_17_carry_out));
  Full_adder full_adder_18 (
    .Carry_in(full_adder_17_carry_out), .A(A[11]), .B(B[11]), .Result(Result[17]),
    .Carry_out(full_adder_18_carry_out));
  Full_adder full_adder_19 (
    .Carry_in(full_adder_18_carry_out), .A(A[12]), .B(B[12]), .Result(Result[18]),
    .Carry_out(full_adder_19_carry_out));
  Full_adder full_adder_20 (
    .Carry_in(full_adder_19_carry_out), .A(A[13]), .B(B[13]), .Result(full_adder_20_result),
    .Carry_out(full_adder_20_carry_out));
  Full_adder full_adder_21 (
    .Carry_in(full_adder_20_carry_out), .A(A[14]), .B(B[14]), .Result(full_adder_21_result),
    .Carry_out(full_adder_21_carry_out));
  Full_adder full_adder_22 (
    .Carry_in(full_adder_21_carry_out), .A(A[15]), .B(B[15]), .Result(full_adder_22_result),
    .Carry_out(full_adder_22_carry_out));
  Full_adder full_adder_23 (
    .Carry_in(full_adder_22_carry_out), .A(A[16]), .B(B[16]), .Result(full_adder_23_result),
    .Carry_out(full_adder_23_carry_out));
  Full_adder full_adder_24 (
    .Carry_in(full_adder_23_carry_out), .A(A[17]), .B(B[17]), .Result(full_adder_24_result),
    .Carry_out(full_adder_24_carry_out));
  Full_adder full_adder_25 (
    .Carry_in(full_adder_24_carry_out), .A(A[18]), .B(B[18]), .Result(full_adder_25_result), .Carry_out(Carry));
endmodule

module _19_bit_xor (
  input  Control,
  input  [18:0] B,
  output [18:0] Result
);

  wire undriven, undriven_2, undriven_3, undriven_4, undriven_5, undriven_6, undriven_7, undriven_8,
       undriven_9, undriven_10, undriven_11, undriven_12, xor_19_out, xor_20_out, xor_21_out, xor_22_out,
       xor_23_out, xor_24_out;
  wire [18:0] bit_extender_1_out;

  assign bit_extender_1_out = {{18{Control}}, Control};  // Bit_Extender bit_extender_1
  xor xor_1 (Result[0], undriven, undriven_7);
  xor xor_2 (Result[1], undriven_2, undriven_10);
  xor xor_3 (Result[2], undriven_3, undriven_8);
  xor xor_4 (Result[3], undriven_11, undriven_4);
  xor xor_5 (Result[4], undriven_5, undriven_9);
  xor xor_6 (Result[5], undriven_6, undriven_12);
  xor xor_7 (Result[6], bit_extender_1_out[0], B[0]);
  xor xor_8 (Result[7], bit_extender_1_out[1], B[1]);
  xor xor_9 (Result[8], bit_extender_1_out[2], B[2]);
  xor xor_10 (Result[9], bit_extender_1_out[3], B[3]);
  xor xor_11 (Result[10], bit_extender_1_out[4], B[4]);
  xor xor_12 (Result[11], bit_extender_1_out[5], B[5]);
  xor xor_13 (Result[12], bit_extender_1_out[6], B[6]);
  xor xor_14 (Result[13], bit_extender_1_out[7], B[7]);
  xor xor_15 (Result[14], bit_extender_1_out[8], B[8]);
  xor xor_16 (Result[16], bit_extender_1_out[10], B[10]);
  xor xor_17 (Result[17], bit_extender_1_out[11], B[11]);
  xor xor_18 (Result[18], bit_extender_1_out[12], B[12]);
  xor xor_19 (xor_19_out, bit_extender_1_out[13], B[13]);
  xor xor_20 (xor_20_out, bit_extender_1_out[14], B[14]);
  xor xor_21 (xor_21_out, bit_extender_1_out[15], B[15]);
  xor xor_22 (xor_22_out, bit_extender_1_out[16], B[16]);
  xor xor_23 (xor_23_out, bit_extender_1_out[17], B[17]);
  xor xor_24 (xor_24_out, bit_extender_1_out[18], B[18]);
  xor xor_25 (Result[15], bit_extender_1_out[9], B[9]);
endmodule

// 19-bit \nADD/SUB
module Add_sub (
  input  Sub,
  input  [18:0] A,
  input  [18:0] B,
  output [18:0] Result,
  output Carry,
  output Overflow
);

  wire and_1_out, and_2_out, n24th_bit_out_1__24th_bit, n24th_bit_out_2__24th_bit, n24th_bit_out_3__24th_bit,
       not_1_out, not_2_out, not_3_out;
  wire [18:0] n19_bit_xor_1_result;

  _24th_bit_out u_24th_bit_out_1 (.Input(A), ._24th_bit(n24th_bit_out_1__24th_bit));
  not not_1 (not_1_out, n24th_bit_out_1__24th_bit);
  _24th_bit_out u_24th_bit_out_2 (.Input(B), ._24th_bit(n24th_bit_out_2__24th_bit));
  not not_2 (not_2_out, n24th_bit_out_2__24th_bit);
  _19_bit_xor u_19_bit_xor_1 (.Control(Sub), .Result(n19_bit_xor_1_result), .B(B));
  _19_bit_full_adder_concise u_19_bit_full_adder_concise_1 (
    .A(A), .B(n19_bit_xor_1_result), .Result(Result), .Carry_in(Sub), .Carry(Carry));
  _24th_bit_out u_24th_bit_out_3 (.Input(Result), ._24th_bit(n24th_bit_out_3__24th_bit));
  not not_3 (not_3_out, n24th_bit_out_3__24th_bit);
  and and_1 (and_1_out, not_3_out, n24th_bit_out_2__24th_bit, n24th_bit_out_1__24th_bit);
  and and_2 (and_2_out, not_2_out, not_1_out, n24th_bit_out_3__24th_bit);
  or or_1 (Overflow, and_1_out, and_2_out);
endmodule

// 24th
module _24th_bit_out (
  input  [18:0] Input,
  output _24th_bit
);
endmodule

// Reduce-OR
module _19_bit_reduce_or (
  input  [18:0] Input,
  output Output
);

  wire undriven, undriven_2, undriven_3, undriven_4, undriven_5, undriven_6;

  or or_1 (Output, Input[0], Input[1], Input[2], Input[3], Input[4], Input[5], Input[6], Input[7], Input[8], Input[9], Input[10], Input[11], Input[12], Input[13], Input[14], Input[15], Input[16], Input[17], Input[18], undriven, undriven_2, undriven_3, undriven_4, undriven_5, undriven_6);
endmodule

module _19_bit_ALU (
  input  Control0,
  input  Control1,
  input  Control2,
  input  [18:0] A,
  input  [18:0] B,
  input  Reset,
  input  Clk,
  output [18:0] Upper_25,
  output [18:0] Lower_25,
  output Zero,
  output Negative,
  output Overflow,
  output Carry,
  output [4:0] counter_state
);

  wire n19_bit_reduce_or_1_output;
  wire [18:0] add_sub_1_result, booth_s_multiplier_1_p6, multiplexer_1_out, multiplexer_2_out,
       n19_bit_and_1_result, n19_bit_or_1_result;

  _19_bit_AND u_19_bit_and_1 (.A(A), .B(B), .Result(n19_bit_and_1_result));
  _19_bit_OR u_19_bit_or_1 (.Result(n19_bit_or_1_result), .A(A), .B(B));
  Add_sub add_sub_1 (.Sub(Control0), .A(A), .B(B), .Overflow(Overflow), .Carry(Carry), .Result(add_sub_1_result));
  Multiplexer #(.width(19), .enable("false")) multiplexer_1 (
    .in0(n19_bit_and_1_result), .in1(n19_bit_or_1_result), .out(multiplexer_1_out), .sel(Control0));
  Multiplexer #(.width(19), .enable("false")) multiplexer_2 (
    .in0(multiplexer_1_out), .in1(add_sub_1_result), .out(multiplexer_2_out), .sel(Control1));
  // Booth_s_multiplier booth_s_multiplier_1: pin names not known; wires that end beside it: A, B, Reset, Clk, Upper_25, booth_s_multiplier_1_p6, counter_state
  Multiplexer #(.width(19), .enable("false")) multiplexer_3 (
    .in0(multiplexer_2_out), .in1(booth_s_multiplier_1_p6), .out(Lower_25), .sel(Control2));
  _24th_bit_out u_24th_bit_out_1 (.Input(Lower_25), ._24th_bit(Negative));
  _19_bit_reduce_or u_19_bit_reduce_or_1 (.Input(Lower_25), .Output(n19_bit_reduce_or_1_output));
  not not_1 (Zero, n19_bit_reduce_or_1_output);
endmodule
