// Logisim project Final.circ as structural Verilog: 1 circuit, main circuit PC+ROM
module PC_ROM (
  input  PC_Enable,
  input  [18:0] Imm,
  input  in_3,
  input  [1:0] PC_Src,
  output [11:0] out_5
);

  wire [18:0] adder_1_out, adder_2_out, multiplexer_1_out;
  wire [18:12] register_1_q;

  Register #(.width(19)) register_1 (
    .D(multiplexer_1_out), .en(PC_Enable), .Q({register_1_q, out_5}), .clk(in_3));  // open: clr
  Adder #(.width(19)) adder_1 (.a({register_1_q, out_5}), .b(19'h1), .out(adder_1_out));  // open: cin, cout
  Adder #(.width(19)) adder_2 (.a(adder_1_out), .b(Imm), .out(adder_2_out));  // open: cin, cout
  Multiplexer #(.select(2), .width(19), .enable("false")) multiplexer_1 (
    .in0(adder_1_out), .in1(adder_2_out), .in2(Imm), .out(multiplexer_1_out), .sel(PC_Src));  // open: in3
  ROM #(.addrWidth(12), .dataWidth(19)) rom_1 (.addr(out_5));  // open: data, sel

  // Notes on the sheet:
  //   contents of rom_1 (hex, n*v repeats v):
  //   c840 c840
endmodule
