// Logisim project bus.circ as structural Verilog: 1 circuit, main circuit main
module main (
  input  [18:0] in_1
);

  wire and_1_out, and_2_out, and_3_out, and_4_out, clock_1_out, not_2_out;
  wire [1:0] counter_1_q, not_1_out;
  wire [18:0] multiplexer_1_out, register_1_q, register_2_q, register_3_q, register_4_q, register_5_q;

  Clock clock_1 (.out(clock_1_out));
  Counter #(.width(2), .max('h3), .ongoal("load")) counter_1 (
    .Q(counter_1_q), .clk(clock_1_out));  // open: load, D, count, carry, clr
  not not_1 (not_1_out[0], counter_1_q[0]);
  xor xor_1 (not_1_out[1], counter_1_q[0], counter_1_q[1]);
  not not_2 (not_2_out, counter_1_q[1]);
  and and_1 (and_1_out, not_1_out[0], not_2_out);
  and and_2 (and_2_out, not_1_out[0], counter_1_q[1]);
  and and_3 (and_3_out, not_2_out, counter_1_q[0]);
  and and_4 (and_4_out, counter_1_q[1], counter_1_q[0]);
  Register #(.width(19)) register_1 (
    .D(multiplexer_1_out), .en(and_2_out), .Q(register_1_q), .clk(clock_1_out));  // open: clr
  Multiplexer #(.select(3), .width(19), .enable("false")) multiplexer_1 (
    .in0(register_1_q), .in1(register_2_q), .in2(register_3_q), .in3(register_4_q), .in4(register_5_q),
    .out(multiplexer_1_out), .sel({1'b0, not_1_out}));  // open: in5, in6, in7
  Register #(.width(19)) register_2 (
    .D(multiplexer_1_out), .en(and_1_out), .Q(register_2_q), .clk(clock_1_out));  // open: clr
  Register #(.width(19)) register_3 (.D(in_1), .en(and_4_out), .Q(register_3_q), .clk(clock_1_out));  // open: clr
  Register #(.width(19)) register_4 (
    .D(multiplexer_1_out), .en(and_3_out), .Q(register_4_q), .clk(clock_1_out));  // open: clr
  Register #(.width(19)) register_5 (
    .D(multiplexer_1_out), .en(1'b0), .Q(register_5_q), .clk(clock_1_out));  // open: clr

  // Notes on the sheet:
  //   A
  //   B
  //   C
  //   D
  //   E
endmodule
