// Logisim project full_CPU_19_bit_multi_cycle.circ as structural Verilog: 4 circuits, main circuit main
module main (
  output [18:0] out_1,
  output [4:0] out_2,
  output [2:0] out_3,
  output [2:0] out_4,
  output [2:0] out_5,
  output [18:0] out_6,
  output [18:0] out_7,
  output [18:0] out_8,
  output [18:0] out_9,
  output [18:0] out_10,
  output [18:0] out_11,
  output [18:0] out_12,
  output [18:0] out_13
);

  wire ALUsrc, and_2_out, and_3_out, and_4_out, Branch, clk, clk_control, controlled_buffer_2_out, IRWrite,
       jmp, main_1_p4, MAR_en, MAR_src, MDR_en, MemRead, MemToReg, MemWrite, nor_1_out, not_1_out, not_2_out,
       not_3_out, not_4_out, or_1_out, PC_enable, RegWrite, ZF;
  wire [0:0] and_1_out;
  wire [2:0] ALUop;
  wire [3:0] main_1_p6, opcode;
  wire [5:0] IR_q;
  wire [11:0] pc_rom_1_out_5;
  wire [13:0] bit_extender_2_out;
  wire [18:0] bit_extender_1_out, bit_extender_3_out, IMM, MAR_q, MDR, multiplexer_1_out, multiplexer_2_out,
       multiplexer_3_out, ram_1_data, RD1, register_1_q, registerfile_1_readdata2;

  or or_1 (or_1_out, PC_enable, jmp, and_1_out[0]);
  PC_ROM pc_rom_1 (.PC_enable(or_1_out), .in_2(clk), .PCsrc({jmp, and_1_out[0]}), .Imm(IMM), .out_5(pc_rom_1_out_5));
  and and_1 (and_1_out[0], Branch, ZF);
  Register #(.width(19)) IR (.D(MDR), .en(IRWrite), .Q({opcode, out_4, out_5, out_3, IR_q}), .clk(clk));  // open: clr
  assign bit_extender_1_out = {{7{1'b0}}, pc_rom_1_out_5};  // Bit_Extender bit_extender_1
  Multiplexer #(.width(19), .enable("false")) multiplexer_1 (
    .in0(bit_extender_1_out), .in1(IMM), .out(multiplexer_1_out), .sel(MAR_src));
  assign bit_extender_2_out = {{13{IR_q[5]}}, IR_q[5]};  // Bit_Extender bit_extender_2
  RegisterFile registerfile_1 (
    .ReadAddr1(out_4), .RegWrite(RegWrite), .WriteAddr(out_3), .ReadAddr2(out_5), .ReadData1(RD1),
    .ReadData2(registerfile_1_readdata2), .in_1(multiplexer_3_out), .in_6(clk), .R2(out_8), .R0(out_6),
    .R1(out_7), .R3(out_9), .R4(out_10), .R5(out_11), .R6(out_12), .R7(out_13));
  Register #(.width(19)) MAR (.D(multiplexer_1_out), .en(MAR_en), .Q(MAR_q), .clk(clk));  // open: clr
  not not_1 (not_1_out, opcode[3]);
  Multiplexer #(.width(19), .enable("false")) multiplexer_2 (
    .in0(registerfile_1_readdata2), .in1(IMM), .out(multiplexer_2_out), .sel(ALUsrc));
  and and_2 (and_2_out, opcode[0], opcode[1], opcode[2], not_1_out);
  Multiplexer #(.width(19), .enable("false")) multiplexer_3 (
    .in0(register_1_q), .in1(MDR), .out(multiplexer_3_out), .sel(MemToReg));
  // _19_bit_alu_updated_main main_1: pin names not known; wires that end beside it: ALUop, RD1, multiplexer_2_out, main_1_p4, out_1, {main_1_p6[3], ZF, main_1_p6[1:0]}, out_2, out_2
  assign main_1_p4 = clk_control ? clk : 1'bz;  // Controlled_Buffer controlled_buffer_1
  assign bit_extender_3_out = {{18{1'b0}}, and_2_out};  // Bit_Extender bit_extender_3
  RAM #(.addrWidth(12), .dataWidth(19), .bus("separate")) ram_1 (
    .addr(MAR_q[11:0]), .din(RD1), .data(ram_1_data), .str(MemWrite), .sel(1'b1), .clk(clk), .ld(MemRead),
    .clr(1'b0));
  Subtractor #(.width(19)) subtractor_1 (
    .a({bit_extender_2_out, IR_q[4:0]}), .b(bit_extender_3_out), .out(IMM));  // open: bin, bout
  Register #(.width(19)) register_1 (.D(out_1), .en(1'b1), .Q(register_1_q), .clk(clk));  // open: clr
  and and_3 (and_3_out, nor_1_out, and_4_out);
  T_Flip_Flop t_ff_1 (.clk(and_3_out), .T(1'b1), .Q(clk_control));  // open: Qn, preset, reset, en
  Clock clock_1 (.out(clk));
  nor nor_1 (nor_1_out, out_2[0], out_2[1], out_2[2], out_2[3], out_2[4]);
  not not_2 (not_2_out, ALUop[0]);
  not not_3 (not_3_out, ALUop[1]);
  and and_4 (and_4_out, not_2_out, not_3_out, ALUop[2]);
  Register #(.width(19)) u_MDR (.D(ram_1_data), .en(MDR_en), .Q(MDR), .clk(clk));  // open: clr
  not not_4 (not_4_out, clk_control);
  assign controlled_buffer_2_out = not_4_out ? clk : 1'bz;  // Controlled_Buffer controlled_buffer_2
  ControlUnit controlunit_1 (
    .opcode(opcode), .ALUop(ALUop), .jmp(jmp), .Branch(Branch), .PC_enable(PC_enable), .MemToReg(MemToReg),
    .ALUsrc(ALUsrc), .RegWrite(RegWrite), .MemWrite(MemWrite), .MemRead(MemRead), .IRWrite(IRWrite),
    .clk(controlled_buffer_2_out), .MAR_en(MAR_en), .MDR_en(MDR_en), .MAR_src(MAR_src));

  // Other names for the same wires on the sheet: WriteReg[2:0] = out_3; ReadReg2[2:0] = out_5; ReadReg1[2:0] = out_4;
  //   cnt_state[4:0] = out_2; R0[18:0] = out_6; R1[18:0] = out_7; R2[18:0] = out_8; R3[18:0] = out_9;
  //   R4[18:0] = out_10; R5[18:0] = out_11; R6[18:0] = out_12; R7[18:0] = out_13
endmodule

// Register
module RegisterFile (
  input  [18:0] in_1,
  input  [2:0] ReadAddr1,
  input  RegWrite,
  input  [2:0] WriteAddr,
  input  [2:0] ReadAddr2,
  input  in_6,
  output [18:0] R0,
  output [18:0] R1,
  output [18:0] R2,
  output [18:0] R3,
  output [18:0] ReadData1,
  output [18:0] ReadData2,
  output [18:0] R4,
  output [18:0] R5,
  output [18:0] R6,
  output [18:0] R7
);

  wire and_1_out, and_2_out, and_3_out, and_4_out, and_5_out, and_6_out, and_7_out, and_8_out,
       decoder_1_out0, decoder_1_out1, decoder_1_out2, decoder_1_out3, decoder_1_out4, decoder_1_out5,
       decoder_1_out6, decoder_1_out7;

  Decoder #(.select(3), .enable("false")) decoder_1 (
    .out0(decoder_1_out0), .out1(decoder_1_out1), .out2(decoder_1_out2), .out3(decoder_1_out3),
    .out4(decoder_1_out4), .out5(decoder_1_out5), .out6(decoder_1_out6), .out7(decoder_1_out7),
    .sel(WriteAddr));
  and and_1 (and_1_out, RegWrite, decoder_1_out0);
  and and_2 (and_2_out, RegWrite, decoder_1_out1);
  and and_3 (and_3_out, RegWrite, decoder_1_out2);
  and and_4 (and_4_out, decoder_1_out3, RegWrite);
  and and_5 (and_5_out, RegWrite, decoder_1_out4);
  and and_6 (and_6_out, RegWrite, decoder_1_out5);
  and and_7 (and_7_out, RegWrite, decoder_1_out6);
  and and_8 (and_8_out, decoder_1_out7, RegWrite);
  Register #(.width(19)) register_1 (.D(in_1), .en(and_1_out), .Q(R0), .clk(in_6));  // open: clr
  Register #(.width(19)) register_2 (.D(in_1), .en(and_5_out), .Q(R4), .clk(in_6));  // open: clr
  Register #(.width(19)) register_3 (.D(in_1), .en(and_2_out), .Q(R1), .clk(in_6));  // open: clr
  Register #(.width(19)) register_4 (.D(in_1), .en(and_6_out), .Q(R5), .clk(in_6));  // open: clr
  Register #(.width(19)) register_5 (.D(in_1), .en(and_3_out), .Q(R2), .clk(in_6));  // open: clr
  Register #(.width(19)) register_6 (.D(in_1), .en(and_7_out), .Q(R6), .clk(in_6));  // open: clr
  Register #(.width(19)) register_7 (.D(in_1), .en(and_4_out), .Q(R3), .clk(in_6));  // open: clr
  Register #(.width(19)) register_8 (.D(in_1), .en(and_8_out), .Q(R7), .clk(in_6));  // open: clr
  Multiplexer #(.select(3), .width(19), .enable("false")) multiplexer_1 (
    .in0(R0), .in1(R1), .in2(R2), .in3(R3), .in4(R4), .in5(R5), .in6(R6), .in7(R7), .out(ReadData1),
    .sel(ReadAddr1));
  Multiplexer #(.select(3), .width(19), .enable("false")) multiplexer_2 (
    .in0(R0), .in1(R1), .in2(R2), .in3(R3), .in4(R4), .in5(R5), .in6(R6), .in7(R7), .out(ReadData2),
    .sel(ReadAddr2));

  // Other names for the same wires on the sheet: clk = in_6
endmodule

// PC
module PC_ROM (
  input  PC_enable,
  input  in_2,
  input  [18:0] Imm,
  input  [1:0] PCsrc,
  output [11:0] out_5
);

  wire [11:0] undriven;
  wire [18:0] adder_1_out, adder_2_out, multiplexer_1_out;
  wire [18:12] register_1_q;
  wire [24:0] rom_1_data;

  Register #(.width(19)) register_1 (
    .D(multiplexer_1_out), .en(PC_enable), .Q({register_1_q, out_5}), .clk(in_2));  // open: clr
  Adder #(.width(19)) adder_1 (.a({register_1_q, out_5}), .b(19'h1), .out(adder_1_out));  // open: cin, cout
  Adder #(.width(19)) adder_2 (.a(adder_1_out), .b(Imm), .out(adder_2_out));  // open: cin, cout
  Multiplexer #(.select(2), .width(19), .enable("false")) multiplexer_1 (
    .in0(adder_1_out), .in1(adder_2_out), .in2(Imm), .out(multiplexer_1_out), .sel(PCsrc));  // open: in3
  ROM #(.addrWidth(12), .dataWidth(25)) rom_1 (.addr(undriven), .data(rom_1_data));  // open: sel

  // Notes on the sheet:
  //   contents of rom_1 (hex, n*v repeats v):
  //   100100a 1002005 53000 254000 895000 456000 657000 c38014 a06014 f10002 1e00000 120000d 1e00000
  //   1e00000
endmodule

// CU
module ControlUnit (
  input  clk,
  input  [3:0] opcode,
  output MAR_src,
  output MDR_en,
  output MAR_en,
  output IRWrite,
  output MemRead,
  output MemWrite,
  output RegWrite,
  output ALUsrc,
  output jmp,
  output Branch,
  output PC_enable,
  output MemToReg,
  output [2:0] ALUop
);

  wire rst;
  wire [2:0] counter_1_q;

  Counter #(.width(3), .max('h7)) counter_1 (.Q(counter_1_q), .clk(clk), .clr(rst));  // open: load, D, count, carry
  ROM #(.addrWidth(7), .dataWidth(16)) rom_1 (
    .addr({counter_1_q, opcode}),
    .data({rst, ALUop, jmp, Branch, PC_enable, MemToReg, ALUsrc, RegWrite, MemWrite, MemRead, IRWrite, MAR_en, MDR_en, MAR_src}));  // open: sel

  // Notes on the sheet:
  //   0000-and
  //   0001-or
  //   0010-add
  //   0011-sub
  //   0100-mul
  //   0101-load
  //   0110-store
  //   0111-beq
  //   1000-addi
  //   1001-jump
  //   1111-hlt
  //   contents of rom_1 (hex, n*v repeats v):
  //   10*4 5*0 4
endmodule
