// Logisim project memory.circ as structural Verilog: 1 circuit, main circuit main
module main (
  input  [7:0] in_1,
  input  in_2,
  input  [7:0] in_3,
  input  in_4,
  input  [3:0] in_5,
  input  in_6,
  output [7:0] out_7,
  output [7:0] out_8,
  output [3:0] out_9,
  output [3:0] out_10,
  output [3:0] out_11
);

  ROM rom_1 (.addr(in_3), .data(out_8), .sel(in_4));
  RAM ram_1 (.addr(in_1), .data(out_7), .ld(in_2));  // open: sel, clk, clr
  RAM #(.addrWidth(4), .dataWidth(4)) ram_2 (.addr(in_5), .data(out_9));  // open: sel, clk, ld, clr
  ROM #(.addrWidth(4), .dataWidth(4)) rom_2 (.addr(in_5), .data(out_11));  // open: sel
  Multiplexer #(.width(4), .enable("false")) multiplexer_1 (.in0(out_9), .in1(out_11), .out(out_10), .sel(in_6));

  // Notes on the sheet:
  //   contents of rom_1 (hex, n*v repeats v):
  //   9*0 67
endmodule
