// Logisim project rom.circ as structural Verilog: 2 circuits, main circuit main
module main (
  input  in_1,
  input  in_2,
  input  reset,
  input  in_4,
  input  [18:0] in_5
);

  wire clock_1_out;
  wire [9:0] control_1_out_3;
  wire [18:0] A_q, B_q, BUS, C_q, controlled_buffer_1_out, controlled_buffer_3_out, controlled_buffer_4_out,
       controlled_buffer_8_out, D_q, E_q;

  Control control_1 (.clk(clock_1_out), .reset(reset), .out_3(control_1_out_3));
  Clock clock_1 (.out(clock_1_out));
  Register #(.width(19)) A (.D(controlled_buffer_4_out), .en(in_1), .Q(A_q), .clk(clock_1_out), .clr(in_2));
  assign controlled_buffer_1_out = control_1_out_3[2] ? BUS : 19'bz;  // Controlled_Buffer controlled_buffer_1
  Register #(.width(19)) B (.D(controlled_buffer_1_out), .en(in_1), .Q(B_q), .clk(clock_1_out), .clr(in_2));
  assign in_5 = control_1_out_3[4] ? BUS : 19'bz;  // Controlled_Buffer controlled_buffer_2
  Register #(.width(19)) C (.D(in_5), .en(in_4), .Q(C_q), .clk(clock_1_out), .clr(in_2));
  assign controlled_buffer_3_out = control_1_out_3[6] ? BUS : 19'bz;  // Controlled_Buffer controlled_buffer_3
  Register #(.width(19)) D (.D(controlled_buffer_3_out), .en(in_1), .Q(D_q), .clk(clock_1_out), .clr(in_2));
  Register #(.width(19)) E (.D(controlled_buffer_8_out), .en(in_1), .Q(E_q), .clk(clock_1_out));  // open: clr
  assign controlled_buffer_4_out = control_1_out_3[0] ? BUS : 19'bz;  // Controlled_Buffer controlled_buffer_4
  assign BUS = control_1_out_3[3] ? B_q : 19'bz;  // Controlled_Buffer controlled_buffer_5
  assign BUS = control_1_out_3[5] ? C_q : 19'bz;  // Controlled_Buffer controlled_buffer_6
  assign BUS = control_1_out_3[7] ? D_q : 19'bz;  // Controlled_Buffer controlled_buffer_7
  assign controlled_buffer_8_out = control_1_out_3[8] ? BUS : 19'bz;  // Controlled_Buffer controlled_buffer_8
  assign BUS = control_1_out_3[9] ? E_q : 19'bz;  // Controlled_Buffer controlled_buffer_9
  assign BUS = control_1_out_3[1] ? A_q : 19'bz;  // Controlled_Buffer controlled_buffer_10
endmodule

module Control (
  input  clk,
  input  reset,
  output [9:0] out_3
);

  wire [1:0] counter_1_q;

  Counter #(.width(2), .max('h3)) counter_1 (
    .count(1'b1), .Q(counter_1_q), .clk(clk), .clr(reset));  // open: load, D, carry
  ROM #(.addrWidth(2), .dataWidth(10)) rom_1 (.addr(counter_1_q), .data(out_3));  // open: sel

  // Notes on the sheet:
  //   contents of rom_1 (hex, n*v repeats v):
  //   24 48 81 12
endmodule
